// Logisim project CPU.circ as structural Verilog: 1 circuit, main circuit main
module main (
  input  in_1,
  input  in_2,
  input  in_3,
  input  in_4,
  input  in_5,
  input  in_6,
  input  in_7,
  input  in_8,
  input  in_9,
  input  in_10,
  input  in_11,
  input  in_12,
  input  in_13,
  input  in_14,
  input  in_15,
  input  in_16,
  input  in_17,
  input  in_18
);

  wire Clk, MAR_p7;
  wire [7:0] controlled_buffer_1_out, controlled_buffer_4_out, lTMP_dout;
  wire [15:0] PC_p7, SP_p7;
  wire [15:8] SP_p3;

  Clock clock_1 (.out(Clk));
  _8bitReg lTMP (
    .Load(in_3), .Din(controlled_buffer_4_out), .Clk(Clk), .nCarryIn(1'b1), .Reset(in_1), .Dout(lTMP_dout));  // open: Up_nDown
  // Probe on lTMP_dout
  assign controlled_buffer_1_out = in_2 ? lTMP_dout : 8'bz;  // Controlled_Buffer controlled_buffer_1
  // Probe on SP_p7
  // _16bitReg SP: pin names not known; wires that end beside it: in_7, in_5, {SP_p3, controlled_buffer_1_out}, in_6, Clk, in_1, SP_p7
  assign {SP_p3, controlled_buffer_1_out} = in_4 ? SP_p7 : 16'bz;  // Controlled_Buffer controlled_buffer_2
  assign SP_p3 = in_14 ? controlled_buffer_4_out : 8'bz;  // Controlled_Buffer controlled_buffer_3
  assign controlled_buffer_4_out = in_15 ? SP_p3 : 8'bz;  // Controlled_Buffer controlled_buffer_4
  // Probe on PC_p7
  // _16bitReg PC: pin names not known; wires that end beside it: in_11, in_9, {SP_p3, controlled_buffer_1_out}, in_10, Clk, in_1, PC_p7
  assign controlled_buffer_1_out = in_12 ? controlled_buffer_4_out : 8'bz;  // Controlled_Buffer controlled_buffer_5
  assign {SP_p3, controlled_buffer_1_out} = in_8 ? PC_p7 : 16'bz;  // Controlled_Buffer controlled_buffer_6
  assign controlled_buffer_4_out = in_13 ? controlled_buffer_1_out : 8'bz;  // Controlled_Buffer controlled_buffer_7
  // Probe on MAR_p7
  // _16bitReg MAR: pin names not known; wires that end beside it: in_18, in_16, {SP_p3, controlled_buffer_1_out}, in_17, Clk, in_1, MAR_p7

  // Other names for the same wires on the sheet: AhD = in_15; AlD = in_13; DAh = in_14; DAl = in_12; lTMPena = in_2;
  //   lTMPload = in_3; MAR_nCarry = in_17; MARload = in_16; MARu_nd = in_18; PC_nCarry = in_10; PCena = in_8;
  //   PCload = in_9; PCu_nd = in_11; Rst = in_1; SP_nCarry = in_6; SPena = in_4; SPload = in_5; SPu_nd = in_7
endmodule
